// Logisim project Project3Given.circ as structural Verilog: 9 circuits, main circuit CPU15
module main (
  input  EnableBreakpoint,
  input  [14:0] Breakpoint
);

  wire and_2_out, and_3_out, chipset_1_irq, CLK, clock_1_out, cpu15_1_c, cpu15_1_e, cpu15_1_i, cpu15_1_n,
       cpu15_1_o, cpu15_1_z, KBCLR, KBIRQ, KBRD, MEMCS, nand_1_out, RE, TTYCLR, TTYWE, WE;
  wire [6:0] KBDATA, TTYDATA;
  wire [7:0] cpu15_1_srf;
  wire [14:0] ADDR, chipset_1_ivect, chipset_1_led0, chipset_1_led1, chipset_1_led2, chipset_1_led3,
       chipset_1_led4, chipset_1_led5, chipset_1_led6, chipset_1_led7, chipset_1_led8, chipset_1_led9,
       chipset_1_leda, chipset_1_ledb, chipset_1_ledc, chipset_1_ledd, chipset_1_lede, cpu15_1_ib,
       cpu15_1_pc, cpu15_1_r0, cpu15_1_r1, cpu15_1_r2, cpu15_1_r3, cpu15_1_r4, cpu15_1_r5, cpu15_1_r6,
       cpu15_1_r7, cpu15_1_srp, DATA, xnor_1_out;

  Clock clock_1 (.out(clock_1_out));
  nand nand_1 (nand_1_out, EnableBreakpoint, xnor_1_out[0], xnor_1_out[1], xnor_1_out[2], xnor_1_out[3], xnor_1_out[4], xnor_1_out[5], xnor_1_out[6], xnor_1_out[7], xnor_1_out[8], xnor_1_out[9], xnor_1_out[10], xnor_1_out[11], xnor_1_out[12], xnor_1_out[13], xnor_1_out[14], 1'b1);
  and and_1 (CLK, clock_1_out, nand_1_out);
  assign xnor_1_out = ~(Breakpoint ^ cpu15_1_pc);  // XNOR_Gate xnor_1, 15 bits wide
  LED I (.in(cpu15_1_i));
  LED Z (.in(cpu15_1_z));
  LED N (.in(cpu15_1_n));
  LED O (.in(cpu15_1_o));
  LED C (.in(cpu15_1_c));
  LED E (.in(cpu15_1_e));
  and and_2 (and_2_out, WE, MEMCS);
  and and_3 (and_3_out, MEMCS, RE);
  RAM #(.addrWidth(15), .asyncread("true"), .dataWidth(15), .databus("bidir")) ram_1 (
    .addr(ADDR), .we(and_2_out), .oe(and_3_out), .clk(CLK), .data(DATA));
  // Probe on cpu15_1_pc
  // Probe on cpu15_1_ib
  // Probe on cpu15_1_srp
  // Probe on cpu15_1_srf
  // Probe on cpu15_1_r0
  // Probe on cpu15_1_r1
  // Probe on cpu15_1_r2
  // Probe on cpu15_1_r3
  // Probe on cpu15_1_r4
  // Probe on cpu15_1_r5
  // Probe on cpu15_1_r6
  // Probe on cpu15_1_r7
  CPU15 cpu15_1 (
    .I(cpu15_1_i), .Z(cpu15_1_z), .N(cpu15_1_n), .O(cpu15_1_o), .C(cpu15_1_c), .E(cpu15_1_e),
    .PC(cpu15_1_pc), .IB(cpu15_1_ib), .SRP(cpu15_1_srp), .SRF(cpu15_1_srf), .R0(cpu15_1_r0), .R1(cpu15_1_r1),
    .R2(cpu15_1_r2), .R3(cpu15_1_r3), .R4(cpu15_1_r4), .R5(cpu15_1_r5), .R6(cpu15_1_r6), .R7(cpu15_1_r7),
    .CLK(CLK), .IRQ(chipset_1_irq), .RE(RE), .WE(WE), .ADDR(ADDR), .DATAIN(DATA), .DATAOUT(DATA));
  // Probe on ADDR
  // Probe on DATA
  // Probe on chipset_1_ivect
  // Probe on TTYDATA
  CHIPSET chipset_1 (
    .RE(RE), .WE(WE), .ADDR(ADDR), .CPUDATAIN(DATA), .CPUDATAOUT(DATA), .IRQ(chipset_1_irq),
    .IVECT(chipset_1_ivect), .CLK(CLK), .MEMCS(MEMCS), .TTYWR(TTYWE), .TTYCLR(TTYCLR), .TTYDATA(TTYDATA),
    .KBRD(KBRD), .KBCLR(KBCLR), .KBIRQ(KBIRQ), .KBDATA(KBDATA), .LED0(chipset_1_led0), .LED1(chipset_1_led1),
    .LED2(chipset_1_led2), .LED3(chipset_1_led3), .LED4(chipset_1_led4), .LED5(chipset_1_led5),
    .LED6(chipset_1_led6), .LED7(chipset_1_led7), .LED8(chipset_1_led8), .LED9(chipset_1_led9),
    .LEDA(chipset_1_leda), .LEDB(chipset_1_ledb), .LEDC(chipset_1_ledc), .LEDD(chipset_1_ledd),
    .LEDE(chipset_1_lede));
  TTY tty_1 (.data(TTYDATA), .clk(CLK), .we(TTYWE), .clr(TTYCLR));
  Keyboard keyboard_1 (.clk(CLK), .re(KBRD), .clr(KBCLR), .avail(KBIRQ), .data(KBDATA));
  DotMatrix #(.matrixcols(15), .matrixrows(15)) dotmatrix_1 (
    .col0(chipset_1_led0), .col1(chipset_1_led1), .col2(chipset_1_led2), .col3(chipset_1_led3),
    .col4(chipset_1_led4), .col5(chipset_1_led5), .col6(chipset_1_led6), .col7(chipset_1_led7),
    .col8(chipset_1_led8), .col9(chipset_1_led9), .col10(chipset_1_leda), .col11(chipset_1_ledb),
    .col12(chipset_1_ledc), .col13(chipset_1_ledd), .col14(chipset_1_lede));
endmodule

// CPU
module CPU15 (
  input  [14:0] DATAIN,
  input  CLK,
  input  IRQ,
  output [14:0] PC,
  output [14:0] IB,
  output [14:0] SRP,
  output [7:0] SRF,
  output [14:0] R0,
  output [14:0] R1,
  output [14:0] R2,
  output [14:0] R3,
  output [14:0] R4,
  output [14:0] R5,
  output [14:0] R6,
  output [14:0] R7,
  output RE,
  output WE,
  output I,
  output Z,
  output [14:0] ADDR,
  output N,
  output O,
  output C,
  output E,
  output [14:0] DATAOUT
);

  wire and_1_out, and_2_out, and_3_out, and_4_out, LOAD, N_C, N_N, N_O, N_Z, not_2_out, NOT_S, or_2_out, PC0,
       PC1, PC2, PC3, PC4, PC5, PC6, PC7, PC8, PC9, PC10, PC11, PC12, PC13, PC14, REGW, S, SRFW, SRPW, STORE,
       SWI, t_ff_1_qn, t_ff_2_qn, t_ff_3_qn, t_ff_4_qn, t_ff_5_qn, t_ff_6_qn, t_ff_7_qn, t_ff_8_qn,
       t_ff_9_qn, t_ff_10_qn, t_ff_11_qn, t_ff_12_qn, t_ff_13_qn, t_ff_14_qn, undriven;
  wire [1:0] ASEL, BSEL, FLAGSRC;
  wire [2:0] ALUOP, REGDATASRC;
  wire [7:0] FLAGWM, multiplexer_3_out;
  wire [7:4] Set_Flags;
  wire [14:0] imm15_1_sext, multiplexer_2_out, multiplexer_4_out, multiplexer_5_out, PC_INIT, regs15_1_a,
       regs15_1_b, Result, undriven_2;

  D_Flip_Flop d_ff_1 (.D(NOT_S), .clk(CLK), .Q(S), .Qn(NOT_S));  // open: preset, reset
  or or_1 (RE, NOT_S, LOAD);
  Register #(.width(15)) register_1 (.D(PC_INIT), .Q(PC), .clk(CLK));  // open: en, clr
  Multiplexer #(.enable("true"), .select(2), .width(15)) multiplexer_1 (
    .in1(PC), .in3(Result), .out(ADDR), .sel({LOAD, RE}), .en(or_2_out));  // open: in0, in2
  DECODE15 decode15_1 (
    .OPCODE(IB[4:0]), .SWI(SWI), .STORE(STORE), .LOAD(LOAD), .ASEL(ASEL), .BSEL(BSEL), .ALUOP(ALUOP),
    .REGDATASRC(REGDATASRC), .REGW(REGW), .FLAGSRC(FLAGSRC), .FLAGWM(FLAGWM), .SRPW(SRPW), .SRFW(SRFW));
  or or_2 (or_2_out, RE, and_1_out);
  and and_1 (and_1_out, LOAD, S);
  buf and_2 (and_2_out, RE);  // AND_Gate
  // NOT_Gate not_1 has open pins: in=LOAD, out=open
  Register #(.width(15)) register_2 (.D(DATAIN), .en(and_2_out), .Q(IB), .clk(CLK));  // open: clr
  Counter #(.max('h7fff), .width(15)) counter_1 (
    .load(undriven), .up(S), .count(S), .clk(S), .D(undriven_2), .Q(PC_INIT));  // open: clr, carry
  Multiplexer #(.enable("true"), .select(3), .width(15)) multiplexer_2 (
    .in0(Result), .in1(DATAIN), .out(multiplexer_2_out), .sel(REGDATASRC), .en(not_2_out));  // open: in2, in3, in4, in5, in6, in7
  not not_2 (not_2_out, STORE);
  and and_3 (and_3_out, S, REGW);
  Multiplexer #(.select(2), .width(8)) multiplexer_3 (
    .in0({4'b0000, N_C, N_O, N_N, N_Z}), .out(multiplexer_3_out), .sel(FLAGSRC));  // open: in1, in2, in3
  FLAGS8 flags8_1 (
    .NF(multiplexer_3_out), .WM(FLAGWM), .CLK(CLK), .IRQ(IRQ),
    .F({Set_Flags[7], I, E, Set_Flags[4], O, C, N, Z}));
  REGS15 regs15_1 (
    .D(multiplexer_2_out), .W(and_3_out), .SelD(IB[7:5]), .CLK(CLK), .SelA(IB[10:8]), .SelB(IB[13:11]),
    .R0(R0), .R1(R1), .R2(R2), .R3(R3), .R4(R4), .R5(R5), .R6(R6), .R7(R7), .A(regs15_1_a), .B(regs15_1_b));
  IMM15 imm15_1 (.INST(IB), .SEXT(imm15_1_sext));
  Multiplexer #(.select(2), .width(15)) multiplexer_4 (
    .in0(regs15_1_b), .in1(imm15_1_sext), .out(multiplexer_4_out), .sel(BSEL));  // open: in2, in3
  Multiplexer #(.select(2), .width(15)) multiplexer_5 (
    .in0(regs15_1_a), .in1({15{1'b0}}), .out(multiplexer_5_out), .sel(ASEL));  // open: in2, in3
  assign DATAOUT = and_4_out ? regs15_1_b : 15'bz;  // Controlled_Buffer controlled_buffer_1
  and and_4 (and_4_out, 1'b0, STORE);
  T_Flip_Flop t_ff_1 (.T(1'b1), .clk(S), .Q(PC0), .Qn(t_ff_1_qn));  // open: reset, preset
  ALU15 alu15_1 (
    .A(multiplexer_5_out), .B(multiplexer_4_out), .OIN(O), .OP(ALUOP), .CIN(C), .R(Result), .C(N_C), .O(N_O),
    .N(N_N), .Z(N_Z));
  T_Flip_Flop t_ff_2 (.T(1'b1), .clk(t_ff_1_qn), .Q(PC1), .Qn(t_ff_2_qn));  // open: reset, preset
  T_Flip_Flop t_ff_3 (.T(1'b1), .clk(t_ff_2_qn), .Q(PC2), .Qn(t_ff_3_qn));  // open: reset, preset
  T_Flip_Flop t_ff_4 (.T(1'b1), .clk(t_ff_3_qn), .Q(PC3), .Qn(t_ff_4_qn));  // open: reset, preset
  T_Flip_Flop t_ff_5 (.T(1'b1), .clk(t_ff_4_qn), .Q(PC4), .Qn(t_ff_5_qn));  // open: reset, preset
  T_Flip_Flop t_ff_6 (.T(1'b1), .clk(t_ff_5_qn), .Q(PC5), .Qn(t_ff_6_qn));  // open: reset, preset
  T_Flip_Flop t_ff_7 (.T(1'b1), .clk(t_ff_6_qn), .Q(PC6), .Qn(t_ff_7_qn));  // open: reset, preset
  T_Flip_Flop t_ff_8 (.T(1'b1), .clk(t_ff_7_qn), .Q(PC7), .Qn(t_ff_8_qn));  // open: reset, preset
  T_Flip_Flop t_ff_9 (.T(1'b1), .clk(t_ff_8_qn), .Q(PC8), .Qn(t_ff_9_qn));  // open: reset, preset
  T_Flip_Flop t_ff_10 (.T(1'b1), .clk(t_ff_9_qn), .Q(PC9), .Qn(t_ff_10_qn));  // open: reset, preset
  T_Flip_Flop t_ff_11 (.T(1'b1), .clk(t_ff_10_qn), .Q(PC10), .Qn(t_ff_11_qn));  // open: reset, preset
  T_Flip_Flop t_ff_12 (.T(1'b1), .clk(t_ff_11_qn), .Q(PC11), .Qn(t_ff_12_qn));  // open: reset, preset
  T_Flip_Flop t_ff_13 (.T(1'b1), .clk(t_ff_12_qn), .Q(PC12), .Qn(t_ff_13_qn));  // open: reset, preset
  T_Flip_Flop t_ff_14 (.T(1'b1), .clk(t_ff_13_qn), .Q(PC13), .Qn(t_ff_14_qn));  // open: reset, preset
  T_Flip_Flop t_ff_15 (.T(1'b1), .clk(t_ff_14_qn), .Q(PC14));  // open: Qn, reset, preset

  assign WE = 1'b0;

  // Other names for the same wires on the sheet: DATA[14:0] = DATAIN; OPCODE[4:0] = IB[4:0]; RD[2:0] = IB[7:5];
  //   RS1[2:0] = IB[10:8]; RS2[2:0] = IB[13:11]; NF[3:0] = {N_C, N_O, N_N, N_Z}; RT0 = Result[0]; RT1 = Result[1];
  //   RT2 = Result[2]; RS3 = Result[3]; RS4 = Result[4]; RT5 = Result[5]; RT6 = Result[6]; RT7 = Result[7];
  //   RT8 = Result[8]; RT9 = Result[9]; RT10 = Result[10]; RT11 = Result[11]; RT12 = Result[12]; RT13 = Result[13];
  //   RT14 = Result[14]; Set_Flags (some bits) = {I, E, O, C, N, Z}

  // Notes on the sheet:
  //   FlipFlop for 2 states
  //   Register Data
  //   Fetch State Processes
  //   Write State Processes
endmodule

module CHIPSET (
  input  RE,
  input  WE,
  input  [14:0] ADDR,
  input  [14:0] CPUDATAIN,
  input  KBIRQ,
  input  [6:0] KBDATA,
  input  CLK,
  output MEMCS,
  output TTYWR,
  output [14:0] IVECT,
  output TTYCLR,
  output [6:0] TTYDATA,
  output KBRD,
  output KBCLR,
  output [14:0] CPUDATAOUT,
  output IRQ,
  output [14:0] LED0,
  output [14:0] LED1,
  output [14:0] LED2,
  output [14:0] LED3,
  output [14:0] LED4,
  output [14:0] LED5,
  output [14:0] LED6,
  output [14:0] LED7,
  output [14:0] LED8,
  output [14:0] LED9,
  output [14:0] LEDA,
  output [14:0] LEDB,
  output [14:0] LEDC,
  output [14:0] LEDD,
  output [14:0] LEDE
);

  wire and_1_out, and_8_out, and_10_out, DATA7, IOCS, IVECTADDR, IVECTEN, IVECTRE, KBCS, LED0EN, LED0END,
       LED1EN, LED1END, LED2EN, LED2END, LED3EN, LED3END, LED4EN, LED4END, LED5EN, LED5END, LED6EN, LED6END,
       LED7EN, LED7END, LED8EN, LED8END, LED9EN, LED9END, LEDAEN, LEDAEND, LEDBEN, LEDBEND, LEDCEN, LEDCEND,
       LEDCS, LEDDEN, LEDDEND, LEDEEN, LEDEEND, LEDFEND, LEDRE, multiplexer_17_out, multiplexer_18_out, RWE,
       TTYCS;
  wire [14:0] DATAL0, DATAL1, DATAL2, DATAL3, DATAL4, DATAL5, DATAL6, DATAL7, DATAL8, DATAL9, DATALA, DATALB,
       DATALC, DATALD, DATALE, LEDDATA;
  wire [14:8] KBDATA15;

  assign CPUDATAOUT = KBRD ? {KBDATA15, DATA7, KBDATA} : 15'bz;  // Controlled_Buffer controlled_buffer_1
  assign CPUDATAOUT = LEDRE ? LEDDATA : 15'bz;  // Controlled_Buffer controlled_buffer_2
  assign CPUDATAOUT = IVECTRE ? IVECT : 15'bz;  // Controlled_Buffer controlled_buffer_3
  Register #(.width(15)) register_1 (.D(DATAL0), .en(LED0EN), .Q(LED0), .clk(CLK));  // open: clr
  Register #(.width(15)) register_2 (.D(DATAL1), .en(LED1EN), .Q(LED1), .clk(CLK));  // open: clr
  Register #(.width(15)) register_3 (.D(DATAL2), .en(LED2EN), .Q(LED2), .clk(CLK));  // open: clr
  Register #(.width(15)) register_4 (.D(DATAL3), .en(LED3EN), .Q(LED3), .clk(CLK));  // open: clr
  Register #(.width(15)) register_5 (.D(DATAL4), .en(LED4EN), .Q(LED4), .clk(CLK));  // open: clr
  and and_1 (and_1_out, WE, LEDCS);
  Decoder #(.select(4)) decoder_1 (
    .out0(LED0END), .out1(LED1END), .out2(LED2END), .out3(LED3END), .out4(LED4END), .out5(LED5END),
    .out6(LED6END), .out7(LED7END), .out8(LED8END), .out9(LED9END), .out10(LEDAEND), .out11(LEDBEND),
    .out12(LEDCEND), .out13(LEDDEND), .out14(LEDEEND), .out15(LEDFEND), .sel(ADDR[3:0]), .en(and_1_out));
  Register #(.width(15)) register_6 (.D(DATAL5), .en(LED5EN), .Q(LED5), .clk(CLK));  // open: clr
  Register #(.width(15)) register_7 (.D(DATAL6), .en(LED6EN), .Q(LED6), .clk(CLK));  // open: clr
  Register #(.width(15)) register_8 (.D(DATAL7), .en(LED7EN), .Q(LED7), .clk(CLK));  // open: clr
  Register #(.width(15)) register_9 (.D(DATAL8), .en(LED8EN), .Q(LED8), .clk(CLK));  // open: clr
  Register #(.width(15)) register_10 (.D(DATAL9), .en(LED9EN), .Q(LED9), .clk(CLK));  // open: clr
  or or_1 (LED0EN, LED0END, LEDFEND);
  or or_2 (LED1EN, LED1END, LEDFEND);
  or or_3 (LED2EN, LED2END, LEDFEND);
  or or_4 (LED3EN, LED3END, LEDFEND);
  or or_5 (LED4EN, LED4END, LEDFEND);
  or or_6 (LED5EN, LED5END, LEDFEND);
  or or_7 (LED6EN, LED6END, LEDFEND);
  or or_8 (LED7EN, LED7END, LEDFEND);
  or or_9 (LED8EN, LED8END, LEDFEND);
  or or_10 (LED9EN, LED9END, LEDFEND);
  or or_11 (LEDAEN, LEDAEND, LEDFEND);
  or or_12 (LEDBEN, LEDBEND, LEDFEND);
  or or_13 (LEDCEN, LEDCEND, LEDFEND);
  or or_14 (LEDDEN, LEDDEND, LEDFEND);
  or or_15 (LEDEEN, LEDEEND, LEDFEND);
  Pull_Resistor pull_resistor_1 (.node(KBDATA15[14]));
  Pull_Resistor pull_resistor_2 (.node(KBDATA15[13]));
  Pull_Resistor pull_resistor_3 (.node(KBDATA15[12]));
  Pull_Resistor pull_resistor_4 (.node(KBDATA15[11]));
  Pull_Resistor pull_resistor_5 (.node(KBDATA15[10]));
  Pull_Resistor pull_resistor_6 (.node(KBDATA15[9]));
  Pull_Resistor pull_resistor_7 (.node(KBDATA15[8]));
  Pull_Resistor pull_resistor_8 (.node(DATA7));
  Register #(.width(15)) register_11 (.D(DATALA), .en(LEDAEN), .Q(LEDA), .clk(CLK));  // open: clr
  Register #(.width(15)) register_12 (.D(DATALB), .en(LEDBEN), .Q(LEDB), .clk(CLK));  // open: clr
  Register #(.width(15)) register_13 (.D(DATALC), .en(LEDCEN), .Q(LEDC), .clk(CLK));  // open: clr
  Register #(.width(15)) register_14 (.D(DATALD), .en(LEDDEN), .Q(LEDD), .clk(CLK));  // open: clr
  Register #(.width(15)) register_15 (.D(DATALE), .en(LEDEEN), .Q(LEDE), .clk(CLK));  // open: clr
  Multiplexer #(.width(15)) multiplexer_1 (.in0(CPUDATAIN), .in1(LED1), .out(DATAL0), .sel(LEDFEND));
  Multiplexer #(.width(15)) multiplexer_2 (.in0(CPUDATAIN), .in1(LED2), .out(DATAL1), .sel(LEDFEND));
  Multiplexer #(.width(15)) multiplexer_3 (.in0(CPUDATAIN), .in1(LED3), .out(DATAL2), .sel(LEDFEND));
  Multiplexer #(.width(15)) multiplexer_4 (.in0(CPUDATAIN), .in1(LED4), .out(DATAL3), .sel(LEDFEND));
  Multiplexer #(.width(15)) multiplexer_5 (.in0(CPUDATAIN), .in1(LED5), .out(DATAL4), .sel(LEDFEND));
  Multiplexer #(.select(4), .width(15)) multiplexer_6 (
    .in0(LED0), .in1(LED1), .in2(LED2), .in3(LED3), .in4(LED4), .in5(LED5), .in6(LED6), .in7(LED7),
    .in8(LED8), .in9(LED9), .in10(LEDA), .in11(LEDB), .in12(LEDC), .in13(LEDD), .in14(LEDE),
    .in15({15{1'b0}}), .out(LEDDATA), .sel(ADDR[3:0]));
  Multiplexer #(.width(15)) multiplexer_7 (.in0(CPUDATAIN), .in1(LED6), .out(DATAL5), .sel(LEDFEND));
  Multiplexer #(.width(15)) multiplexer_8 (.in0(CPUDATAIN), .in1(LED7), .out(DATAL6), .sel(LEDFEND));
  Multiplexer #(.width(15)) multiplexer_9 (.in0(CPUDATAIN), .in1(LED8), .out(DATAL7), .sel(LEDFEND));
  Multiplexer #(.width(15)) multiplexer_10 (.in0(CPUDATAIN), .in1(LED9), .out(DATAL8), .sel(LEDFEND));
  Multiplexer #(.width(15)) multiplexer_11 (.in0(CPUDATAIN), .in1(LEDA), .out(DATAL9), .sel(LEDFEND));
  and and_2 (LEDRE, RE, LEDCS);
  Multiplexer #(.width(15)) multiplexer_12 (.in0(CPUDATAIN), .in1(LEDB), .out(DATALA), .sel(LEDFEND));
  Multiplexer #(.width(15)) multiplexer_13 (.in0(CPUDATAIN), .in1(LEDC), .out(DATALB), .sel(LEDFEND));
  Multiplexer #(.width(15)) multiplexer_14 (.in0(CPUDATAIN), .in1(LEDD), .out(DATALC), .sel(LEDFEND));
  Multiplexer #(.width(15)) multiplexer_15 (.in0(CPUDATAIN), .in1(LEDE), .out(DATALD), .sel(LEDFEND));
  Multiplexer #(.width(15)) multiplexer_16 (.in0(CPUDATAIN), .in1(CPUDATAIN), .out(DATALE), .sel(LEDFEND));
  and and_3 (IOCS, ADDR[5], ADDR[6], ADDR[7], ADDR[8], ADDR[9], ADDR[10], ADDR[11], ADDR[12], ADDR[13], ADDR[14], 1'b1);
  and and_4 (TTYCS, IOCS, ADDR[0], ~ADDR[1], ~ADDR[2], ~ADDR[3], ADDR[4]);  // AND_Gate
  and and_5 (KBCS, IOCS, ~ADDR[0], ~ADDR[1], ~ADDR[2], ~ADDR[3], ADDR[4]);  // AND_Gate
  and and_6 (IVECTADDR, ADDR[0], ADDR[1], ADDR[2], ADDR[3], ADDR[4], ADDR[5], ADDR[6], ADDR[7], ADDR[8], ADDR[9], ADDR[10], ADDR[11], ADDR[12], ADDR[13], ADDR[14]);
  and and_7 (TTYWR, TTYCS, WE);
  and and_8 (and_8_out, TTYWR, DATA7);
  and and_9 (KBRD, KBCS, RE);
  and and_10 (and_10_out, KBCS, WE);
  Multiplexer multiplexer_17 (.in0(and_10_out), .in1(1'b0), .out(multiplexer_17_out), .sel(KBCLR));
  and and_11 (LEDCS, IOCS, ~ADDR[4], RWE);  // AND_Gate
  and and_12 (IVECTEN, IVECTADDR, WE);
  and and_13 (IVECTRE, IVECTADDR, RE);
  or or_16 (RWE, RE, WE);
  and and_14 (MEMCS, ~IOCS, RWE);  // AND_Gate
  Multiplexer multiplexer_18 (.in0(and_8_out), .in1(1'b0), .out(multiplexer_18_out), .sel(TTYCLR));
  D_Flip_Flop d_ff_1 (.clk(CLK), .D(multiplexer_17_out), .Q(KBCLR));  // open: Qn, preset, reset
  Register #(.width(15)) register_16 (.D(CPUDATAIN), .en(IVECTEN), .Q(IVECT), .clk(CLK));  // open: clr
  D_Flip_Flop d_ff_2 (.clk(CLK), .D(multiplexer_18_out), .Q(TTYCLR));  // open: Qn, preset, reset

  assign IRQ = KBIRQ;
  assign TTYDATA = CPUDATAIN[6:0];

  // Other names for the same wires on the sheet: DATA[14:0] = CPUDATAIN; KBDATA15[7:0] = {DATA7, KBDATA}
endmodule

module ADDER15 (
  input  [14:0] A,
  input  [14:0] B,
  input  CIN,
  output COUT,
  output [14:0] S
);

  wire and_1_out, and_2_out, and_3_out, and_4_out, and_5_out, and_6_out, and_7_out, and_8_out, and_9_out,
       and_10_out, and_11_out, and_12_out, and_13_out, and_14_out, and_15_out, and_16_out, and_17_out,
       and_18_out, and_19_out, and_20_out, and_21_out, and_22_out, and_23_out, and_24_out, and_25_out,
       and_26_out, and_27_out, and_28_out, and_29_out, and_30_out, and_31_out, and_32_out, and_33_out,
       and_34_out, and_35_out, and_36_out, and_37_out, and_38_out, and_39_out, and_40_out, and_41_out,
       and_42_out, and_43_out, and_44_out, and_45_out, C0, C1, C2, C3, C4, C5, C6, C7, C8, C9, C10, C11, C12,
       C13, G0, G1, G2, G3, G4, G5, G6, G7, G8, G9, G10, G11, G12, G13, G14, P0, P1, P2, P3, P4, P5, P6, P7,
       P8, P9, P10, P11, P12, P13, P14;

  and and_1 (and_1_out, P0, CIN);
  and and_2 (and_2_out, P5, C4);
  xor xor_1 (S[10], A[10], B[10], C9);
  or or_1 (C10, G10, and_3_out);
  and and_3 (and_3_out, P10, C9);
  xor xor_2 (S[0], A[0], B[0], CIN);
  or or_2 (C0, G0, and_1_out);
  xor xor_3 (S[5], A[5], B[5], C4);
  or or_3 (C5, G5, and_2_out);
  and and_4 (and_4_out, G0, P1);
  and and_5 (and_5_out, P1, P0, CIN);
  and and_6 (and_6_out, P6, G5);
  and and_7 (and_7_out, P6, P5, C4);
  and and_8 (and_8_out, P11, G10);
  and and_9 (and_9_out, P11, P10, C9);
  xor xor_4 (S[1], A[1], B[1], C0);
  or or_4 (C1, G1, and_4_out, and_5_out);
  xor xor_5 (S[6], A[6], B[6], C5);
  or or_5 (C6, G6, and_6_out, and_7_out);
  xor xor_6 (S[11], A[11], B[11], C10);
  or or_6 (C11, G11, and_8_out, and_9_out);
  and and_10 (and_10_out, P2, G1);
  and and_11 (and_11_out, P2, P1, G0);
  and and_12 (and_12_out, P2, P1, P0, CIN);
  and and_13 (and_13_out, P7, G6);
  and and_14 (and_14_out, P7, P6, G5);
  and and_15 (and_15_out, P7, P6, P5, C4);
  and and_16 (and_16_out, P12, G11);
  and and_17 (and_17_out, P12, P11, G10);
  and and_18 (and_18_out, P12, P11, P10, C9);
  xor xor_7 (S[12], A[12], B[12], C11);
  or or_7 (C12, G12, and_16_out, and_17_out, and_18_out);
  xor xor_8 (S[2], A[2], B[2], C1);
  or or_8 (C2, G2, and_10_out, and_11_out, and_12_out);
  xor xor_9 (S[7], A[7], B[7], C6);
  or or_9 (C7, G7, and_13_out, and_14_out, and_15_out);
  and and_19 (and_19_out, P13, G12);
  and and_20 (and_20_out, P13, P12, G11);
  and and_21 (and_21_out, P13, P12, P11, G10);
  and and_22 (and_22_out, P13, P12, P11, P10, C9);
  and and_23 (and_23_out, P3, G2);
  and and_24 (and_24_out, P3, P2, G1);
  and and_25 (and_25_out, P3, P2, P1, G0);
  and and_26 (and_26_out, P3, P2, P1, P0, CIN);
  and and_27 (and_27_out, P8, G7);
  and and_28 (and_28_out, P8, P7, G6);
  and and_29 (and_29_out, P8, P7, P6, G5);
  and and_30 (and_30_out, P8, P7, P6, P5, C4);
  xor xor_10 (S[3], A[3], B[3], C2);
  or or_10 (C3, G3, and_23_out, and_24_out, and_25_out, and_26_out);
  xor xor_11 (S[8], A[8], B[8], C7);
  or or_11 (C8, G8, and_27_out, and_28_out, and_29_out, and_30_out);
  xor xor_12 (S[13], A[13], B[13], C12);
  or or_12 (C13, G13, and_19_out, and_20_out, and_21_out, and_22_out);
  and and_31 (and_31_out, P4, G3);
  and and_32 (and_32_out, P4, P3, G2);
  and and_33 (and_33_out, P4, P3, P2, G1);
  and and_34 (and_34_out, P4, P3, P2, P1, G0);
  and and_35 (and_35_out, P4, P3, P2, P1, P0, CIN);
  and and_36 (and_36_out, P9, G8);
  and and_37 (and_37_out, P9, P8, G7);
  and and_38 (and_38_out, P9, P8, P7, G6);
  and and_39 (and_39_out, P9, P8, P7, P6, G5);
  and and_40 (and_40_out, P9, P8, P7, P6, P5, C4);
  and and_41 (and_41_out, P14, G13);
  and and_42 (and_42_out, P14, P13, G12);
  and and_43 (and_43_out, P14, P13, P12, G11);
  and and_44 (and_44_out, P14, P13, P12, P11, G10);
  and and_45 (and_45_out, P14, P13, P12, P11, P10, C9);
  xor xor_13 (S[4], A[4], B[4], C3);
  or or_13 (C4, G4, and_31_out, and_32_out, and_33_out, and_34_out, and_35_out);
  xor xor_14 (S[9], A[9], B[9], C8);
  or or_14 (C9, G9, and_36_out, and_37_out, and_38_out, and_39_out, and_40_out);
  xor xor_15 (S[14], A[14], B[14], C13);
  or or_15 (COUT, G14, and_41_out, and_42_out, and_43_out, and_44_out, and_45_out);
  and and_46 (G0, A[0], B[0]);
  and and_47 (G1, A[1], B[1]);
  and and_48 (G2, A[2], B[2]);
  and and_49 (G3, A[3], B[3]);
  and and_50 (G4, A[4], B[4]);
  and and_51 (G5, A[5], B[5]);
  and and_52 (G6, A[6], B[6]);
  and and_53 (G7, A[7], B[7]);
  and and_54 (G8, A[8], B[8]);
  and and_55 (G9, A[9], B[9]);
  and and_56 (G10, A[10], B[10]);
  and and_57 (G11, A[11], B[11]);
  and and_58 (G12, A[12], B[12]);
  and and_59 (G13, A[13], B[13]);
  and and_60 (G14, A[14], B[14]);
  or or_16 (P0, A[0], B[0]);
  or or_17 (P1, A[1], B[1]);
  or or_18 (P2, A[2], B[2]);
  or or_19 (P3, A[3], B[3]);
  or or_20 (P4, A[4], B[4]);
  or or_21 (P5, A[5], B[5]);
  or or_22 (P6, A[6], B[6]);
  or or_23 (P7, A[7], B[7]);
  or or_24 (P8, A[8], B[8]);
  or or_25 (P9, A[9], B[9]);
  or or_26 (P10, A[10], B[10]);
  or or_27 (P11, A[11], B[11]);
  or or_28 (P12, A[12], B[12]);
  or or_29 (P13, A[13], B[13]);
  or or_30 (P14, A[14], B[14]);

  // Notes on the sheet:
  //   Bits 0-4
  //   Bits 5-9
  //   Bits 10-14
  //   CLA Logic
  //   CLA Logic
  //   CLA Logic
endmodule

module REGS15 (
  input  [14:0] D,
  input  [2:0] SelA,
  input  [2:0] SelB,
  input  W,
  input  [2:0] SelD,
  input  CLK,
  output [14:0] R0,
  output [14:0] R1,
  output [14:0] R2,
  output [14:0] R3,
  output [14:0] R4,
  output [14:0] R5,
  output [14:0] R6,
  output [14:0] R7,
  output [14:0] A,
  output [14:0] B
);

  wire and_1_out, and_2_out, and_3_out, and_4_out, and_5_out, and_6_out, and_7_out, and_8_out, Reg0, Reg1,
       Reg2, Reg3, Reg4, Reg5, Reg6, Reg7;

  Decoder #(.enable("false"), .select(3)) decoder_1 (
    .out0(Reg0), .out1(Reg1), .out2(Reg2), .out3(Reg3), .out4(Reg4), .out5(Reg5), .out6(Reg6), .out7(Reg7),
    .sel(SelD));
  and and_1 (and_1_out, Reg0, W);
  and and_2 (and_2_out, Reg2, W);
  and and_3 (and_3_out, Reg4, W);
  and and_4 (and_4_out, Reg6, W);
  Register #(.width(15)) register_1 (.D(D), .en(and_1_out), .Q(R0), .clk(CLK));  // open: clr
  Register #(.width(15)) register_2 (.D(D), .en(and_2_out), .Q(R2), .clk(CLK));  // open: clr
  Register #(.width(15)) register_3 (.D(D), .en(and_3_out), .Q(R4), .clk(CLK));  // open: clr
  Register #(.width(15)) register_4 (.D(D), .en(and_4_out), .Q(R6), .clk(CLK));  // open: clr
  Register #(.width(15)) register_5 (.D(D), .en(and_5_out), .Q(R1), .clk(CLK));  // open: clr
  and and_5 (and_5_out, Reg1, W);
  Register #(.width(15)) register_6 (.D(D), .en(and_6_out), .Q(R3), .clk(CLK));  // open: clr
  and and_6 (and_6_out, Reg3, W);
  Register #(.width(15)) register_7 (.D(D), .en(and_7_out), .Q(R5), .clk(CLK));  // open: clr
  and and_7 (and_7_out, Reg5, W);
  Register #(.width(15)) register_8 (.D(D), .en(and_8_out), .Q(R7), .clk(CLK));  // open: clr
  and and_8 (and_8_out, Reg7, W);
  Multiplexer #(.select(3), .width(15)) multiplexer_1 (
    .in0(R0), .in1(R1), .in2(R2), .in3(R3), .in4(R4), .in5(R5), .in6(R6), .in7(R7), .out(A), .sel(SelA));
  Multiplexer #(.select(3), .width(15)) multiplexer_2 (
    .in0(R0), .in1(R1), .in2(R2), .in3(R3), .in4(R4), .in5(R5), .in6(R6), .in7(R7), .out(B), .sel(SelB));

  // Notes on the sheet:
  //   Decoder and Registers
  //   Write Circuit
  //   Read Circuit
endmodule

module ALU15 (
  input  [2:0] OP,
  input  [14:0] A,
  input  [14:0] B,
  input  CIN,
  input  OIN,
  output C,
  output [14:0] R,
  output O,
  output N,
  output Z
);

  wire adder15_2_cout, and_2_out, COUT_ADD, COUT_SLL, COUT_SRA, COUT_SRL, COUT_SUB, xnor_1_out, xor_2_out,
       xor_3_out, xor_4_out, xor_5_out;
  wire [14:0] adder15_1_s, adder15_2_s, and_1_out, Arithmetic_Shift_Right, Logical_Shift_Left,
       Logical_Shift_Right, not_1_out, or_1_out, xor_1_out;

  ADDER15 adder15_1 (.A(A), .B(B), .CIN(CIN), .S(adder15_1_s), .COUT(COUT_ADD));
  assign not_1_out = ~B;  // NOT_Gate not_1, 15 bits wide
  ADDER15 adder15_2 (.A(A), .B(not_1_out), .CIN(1'b1), .S(adder15_2_s), .COUT(adder15_2_cout));
  not not_2 (COUT_SUB, adder15_2_cout);
  assign and_1_out = A & B;  // AND_Gate and_1, 15 bits wide
  assign or_1_out = A | B;  // OR_Gate or_1, 15 bits wide
  assign xor_1_out = A ^ B;  // XOR_Gate xor_1, 15 bits wide
  Multiplexer #(.select(3), .width(15)) multiplexer_1 (
    .in0(adder15_1_s), .in1(adder15_2_s), .in2(and_1_out), .in3(or_1_out), .in4(xor_1_out),
    .in5(Logical_Shift_Left), .in6(Logical_Shift_Right), .in7(Arithmetic_Shift_Right), .out({N, R[13:0]}),
    .sel(OP));
  xor xor_2 (xor_2_out, A[14], N);
  xnor xnor_1 (xnor_1_out, A[14], B[14]);
  xor xor_3 (xor_3_out, A[14], B[14]);
  xor xor_4 (xor_4_out, A[14], N);
  and and_2 (and_2_out, xor_2_out, xnor_1_out);
  xor xor_5 (xor_5_out, xor_3_out, xor_4_out);
  Multiplexer #(.select(3)) multiplexer_2 (
    .in0(and_2_out), .in1(xor_5_out), .out(O), .sel(OP));  // open: in2, in3, in4, in5, in6, in7
  Multiplexer #(.select(4)) multiplexer_3 (
    .in0(A[14]), .in1(A[13]), .in2(A[12]), .in3(A[11]), .in4(A[10]), .in5(A[9]), .in6(A[8]), .in7(A[7]),
    .in8(A[6]), .in9(A[5]), .in10(A[4]), .in11(A[3]), .in12(A[2]), .in13(A[1]), .in14(A[0]), .in15(1'b0),
    .out(Logical_Shift_Left[14]), .sel(B[3:0]));
  Multiplexer #(.select(4)) multiplexer_4 (
    .in0(A[13]), .in1(A[12]), .in2(A[11]), .in3(A[10]), .in4(A[9]), .in5(A[8]), .in6(A[7]), .in7(A[6]),
    .in8(A[5]), .in9(A[4]), .in10(A[3]), .in11(A[2]), .in12(A[1]), .in13(A[0]), .in14(1'b0), .in15(1'b0),
    .out(Logical_Shift_Left[13]), .sel(B[3:0]));
  Multiplexer #(.select(4)) multiplexer_5 (
    .in0(A[12]), .in1(A[11]), .in2(A[10]), .in3(A[9]), .in4(A[8]), .in5(A[7]), .in6(A[6]), .in7(A[5]),
    .in8(A[4]), .in9(A[3]), .in10(A[2]), .in11(A[1]), .in12(A[0]), .in13(1'b0), .in14(1'b0), .in15(1'b0),
    .out(Logical_Shift_Left[12]), .sel(B[3:0]));
  Multiplexer #(.select(4)) multiplexer_6 (
    .in0(A[12]), .in1(A[11]), .in2(A[9]), .in3(A[8]), .in4(A[7]), .in5(A[6]), .in6(A[5]), .in7(A[4]),
    .in8(A[3]), .in9(A[2]), .in10(A[1]), .in11(A[0]), .in12(1'b0), .in13(1'b0), .in14(1'b0), .in15(1'b0),
    .out(Logical_Shift_Left[11]), .sel(B[3:0]));
  Multiplexer #(.select(4)) multiplexer_7 (
    .in0(A[10]), .in1(A[9]), .in2(A[8]), .in3(A[7]), .in4(A[6]), .in5(A[5]), .in6(A[4]), .in7(A[3]),
    .in8(A[2]), .in9(A[1]), .in10(A[0]), .in11(1'b0), .in12(1'b0), .in13(1'b0), .in14(1'b0), .in15(1'b0),
    .out(Logical_Shift_Left[10]), .sel(B[3:0]));
  Multiplexer #(.select(4)) multiplexer_8 (
    .in0(A[9]), .in1(A[8]), .in2(A[7]), .in3(A[6]), .in4(A[5]), .in5(A[4]), .in6(A[3]), .in7(A[2]),
    .in8(A[1]), .in9(A[0]), .in10(1'b0), .in11(1'b0), .in12(1'b0), .in13(1'b0), .in14(1'b0), .in15(1'b0),
    .out(Logical_Shift_Left[9]), .sel(B[3:0]));
  Multiplexer #(.select(4)) multiplexer_9 (
    .in0(A[8]), .in1(A[7]), .in2(A[6]), .in3(A[5]), .in4(A[4]), .in5(A[3]), .in6(A[2]), .in7(A[1]),
    .in8(A[0]), .in9(1'b0), .in10(1'b0), .in11(1'b0), .in12(1'b0), .in13(1'b0), .in14(1'b0), .in15(1'b0),
    .out(Logical_Shift_Left[8]), .sel(B[3:0]));
  Multiplexer #(.select(4)) multiplexer_10 (
    .in0(A[7]), .in1(A[6]), .in2(A[5]), .in3(A[4]), .in4(A[3]), .in5(A[2]), .in6(A[1]), .in7(A[0]),
    .in8(1'b0), .in9(1'b0), .in10(1'b0), .in11(1'b0), .in12(1'b0), .in13(1'b0), .in14(1'b0), .in15(1'b0),
    .out(Logical_Shift_Left[7]), .sel(B[3:0]));
  Multiplexer #(.select(4)) multiplexer_11 (
    .in0(A[6]), .in1(A[5]), .in2(A[4]), .in3(A[3]), .in4(A[2]), .in5(A[1]), .in6(A[0]), .in7(1'b0),
    .in8(1'b0), .in9(1'b0), .in10(1'b0), .in11(1'b0), .in12(1'b0), .in13(1'b0), .in14(1'b0), .in15(1'b0),
    .out(Logical_Shift_Left[6]), .sel(B[3:0]));
  Multiplexer #(.select(4)) multiplexer_12 (
    .in0(A[5]), .in1(A[4]), .in2(A[3]), .in3(A[2]), .in4(A[1]), .in5(A[0]), .in6(1'b0), .in7(1'b0),
    .in8(1'b0), .in9(1'b0), .in10(1'b0), .in11(1'b0), .in12(1'b0), .in13(1'b0), .in14(1'b0), .in15(1'b0),
    .out(Logical_Shift_Left[5]), .sel(B[3:0]));
  Multiplexer #(.select(4)) multiplexer_13 (
    .in0(A[4]), .in1(A[3]), .in2(A[2]), .in3(A[1]), .in4(A[0]), .in5(1'b0), .in6(1'b0), .in7(1'b0),
    .in8(1'b0), .in9(1'b0), .in10(1'b0), .in11(1'b0), .in12(1'b0), .in13(1'b0), .in14(1'b0), .in15(1'b0),
    .out(Logical_Shift_Left[4]), .sel(B[3:0]));
  Multiplexer #(.select(4)) multiplexer_14 (
    .in0(A[3]), .in1(A[2]), .in2(A[1]), .in3(A[0]), .in4(1'b0), .in5(1'b0), .in6(1'b0), .in7(1'b0),
    .in8(1'b0), .in9(1'b0), .in10(1'b0), .in11(1'b0), .in12(1'b0), .in13(1'b0), .in14(1'b0), .in15(1'b0),
    .out(Logical_Shift_Left[3]), .sel(B[3:0]));
  Multiplexer #(.select(4)) multiplexer_15 (
    .in0(A[2]), .in1(A[1]), .in2(A[0]), .in3(1'b0), .in4(1'b0), .in5(1'b0), .in6(1'b0), .in7(1'b0),
    .in8(1'b0), .in9(1'b0), .in10(1'b0), .in11(1'b0), .in12(1'b0), .in13(1'b0), .in14(1'b0), .in15(1'b0),
    .out(Logical_Shift_Left[2]), .sel(B[3:0]));
  Multiplexer #(.select(4)) multiplexer_16 (
    .in0(A[1]), .in1(A[0]), .in2(1'b0), .in3(1'b0), .in4(1'b0), .in5(1'b0), .in6(1'b0), .in7(1'b0),
    .in8(1'b0), .in9(1'b0), .in10(1'b0), .in11(1'b0), .in12(1'b0), .in13(1'b0), .in14(1'b0), .in15(1'b0),
    .out(Logical_Shift_Left[1]), .sel(B[3:0]));
  Multiplexer #(.select(4)) multiplexer_17 (
    .in0(A[0]), .in1(1'b0), .in2(1'b0), .in3(1'b0), .in4(1'b0), .in5(1'b0), .in6(1'b0), .in7(1'b0),
    .in8(1'b0), .in9(1'b0), .in10(1'b0), .in11(1'b0), .in12(1'b0), .in13(1'b0), .in14(1'b0), .in15(1'b0),
    .out(Logical_Shift_Left[0]), .sel(B[3:0]));
  Multiplexer #(.select(3)) multiplexer_18 (
    .in0(COUT_ADD), .in1(COUT_SUB), .in5(COUT_SLL), .in6(COUT_SRL), .in7(COUT_SRA), .out(C), .sel(OP));  // open: in2, in3, in4
  nor nor_1 (Z, N, R[13], R[12], R[11], R[10], R[9], R[8], R[7], R[6], R[5], R[4], R[3], R[2], R[1], R[0]);
  Multiplexer #(.select(4)) multiplexer_19 (
    .in1(A[14]), .in2(A[13]), .in3(A[12]), .in4(A[11]), .in5(A[10]), .in6(A[9]), .in7(A[8]), .in8(A[7]),
    .in9(A[6]), .in10(A[5]), .in11(A[4]), .in12(A[3]), .in13(A[2]), .in14(A[1]), .in15(A[0]), .out(COUT_SLL),
    .sel(B[3:0]));  // open: in0
  Multiplexer #(.select(4)) multiplexer_20 (
    .in0(A[14]), .in1(1'b0), .in2(1'b0), .in3(1'b0), .in4(1'b0), .in5(1'b0), .in6(1'b0), .in7(1'b0),
    .in8(1'b0), .in9(1'b0), .in10(1'b0), .in11(1'b0), .in12(1'b0), .in13(1'b0), .in14(1'b0), .in15(1'b0),
    .out(Logical_Shift_Right[14]), .sel(B[3:0]));
  Multiplexer #(.select(4)) multiplexer_21 (
    .in0(A[13]), .in1(A[14]), .in2(1'b0), .in3(1'b0), .in4(1'b0), .in5(1'b0), .in6(1'b0), .in7(1'b0),
    .in8(1'b0), .in9(1'b0), .in10(1'b0), .in11(1'b0), .in12(1'b0), .in13(1'b0), .in14(1'b0), .in15(1'b0),
    .out(Logical_Shift_Right[13]), .sel(B[3:0]));
  Multiplexer #(.select(4)) multiplexer_22 (
    .in0(A[12]), .in1(A[13]), .in2(A[14]), .in3(1'b0), .in4(1'b0), .in5(1'b0), .in6(1'b0), .in7(1'b0),
    .in8(1'b0), .in9(1'b0), .in10(1'b0), .in11(1'b0), .in12(1'b0), .in13(1'b0), .in14(1'b0), .in15(1'b0),
    .out(Logical_Shift_Right[12]), .sel(B[3:0]));
  Multiplexer #(.select(4)) multiplexer_23 (
    .in0(A[11]), .in1(A[12]), .in2(A[13]), .in3(A[14]), .in4(1'b0), .in5(1'b0), .in6(1'b0), .in7(1'b0),
    .in8(1'b0), .in9(1'b0), .in10(1'b0), .in11(1'b0), .in12(1'b0), .in13(1'b0), .in14(1'b0), .in15(1'b0),
    .out(Logical_Shift_Right[11]), .sel(B[3:0]));
  Multiplexer #(.select(4)) multiplexer_24 (
    .in0(A[10]), .in1(A[11]), .in2(A[12]), .in3(A[13]), .in4(A[14]), .in5(1'b0), .in6(1'b0), .in7(1'b0),
    .in8(1'b0), .in9(1'b0), .in10(1'b0), .in11(1'b0), .in12(1'b0), .in13(1'b0), .in14(1'b0), .in15(1'b0),
    .out(Logical_Shift_Right[10]), .sel(B[3:0]));
  Multiplexer #(.select(4)) multiplexer_25 (
    .in0(A[9]), .in1(A[10]), .in2(A[11]), .in3(A[12]), .in4(A[13]), .in5(A[14]), .in6(1'b0), .in7(1'b0),
    .in8(1'b0), .in9(1'b0), .in10(1'b0), .in11(1'b0), .in12(1'b0), .in13(1'b0), .in14(1'b0), .in15(1'b0),
    .out(Logical_Shift_Right[9]), .sel(B[3:0]));
  Multiplexer #(.select(4)) multiplexer_26 (
    .in0(A[8]), .in1(A[9]), .in2(A[10]), .in3(A[11]), .in4(A[12]), .in5(A[13]), .in6(A[14]), .in7(1'b0),
    .in8(1'b0), .in9(1'b0), .in10(1'b0), .in11(1'b0), .in12(1'b0), .in13(1'b0), .in14(1'b0), .in15(1'b0),
    .out(Logical_Shift_Right[8]), .sel(B[3:0]));
  Multiplexer #(.select(4)) multiplexer_27 (
    .in0(A[7]), .in1(A[8]), .in2(A[9]), .in3(A[10]), .in4(A[11]), .in5(A[12]), .in6(A[13]), .in7(A[14]),
    .in8(1'b0), .in9(1'b0), .in10(1'b0), .in11(1'b0), .in12(1'b0), .in13(1'b0), .in14(1'b0), .in15(1'b0),
    .out(Logical_Shift_Right[7]), .sel(B[3:0]));
  Multiplexer #(.select(4)) multiplexer_28 (
    .in0(A[6]), .in1(A[7]), .in2(A[8]), .in3(A[9]), .in4(A[10]), .in5(A[11]), .in6(A[12]), .in7(A[13]),
    .in8(A[14]), .in9(1'b0), .in10(1'b0), .in11(1'b0), .in12(1'b0), .in13(1'b0), .in14(1'b0), .in15(1'b0),
    .out(Logical_Shift_Right[6]), .sel(B[3:0]));
  Multiplexer #(.select(4)) multiplexer_29 (
    .in0(A[5]), .in1(A[6]), .in2(A[7]), .in3(A[8]), .in4(A[9]), .in5(A[10]), .in6(A[11]), .in7(A[12]),
    .in8(A[13]), .in9(A[14]), .in10(1'b0), .in11(1'b0), .in12(1'b0), .in13(1'b0), .in14(1'b0), .in15(1'b0),
    .out(Logical_Shift_Right[5]), .sel(B[3:0]));
  Multiplexer #(.select(4)) multiplexer_30 (
    .in0(A[4]), .in1(A[5]), .in2(A[6]), .in3(A[7]), .in4(A[8]), .in5(A[9]), .in6(A[10]), .in7(A[11]),
    .in8(A[12]), .in9(A[13]), .in10(A[14]), .in11(1'b0), .in12(1'b0), .in13(1'b0), .in14(1'b0), .in15(1'b0),
    .out(Logical_Shift_Right[4]), .sel(B[3:0]));
  Multiplexer #(.select(4)) multiplexer_31 (
    .in0(A[3]), .in1(A[4]), .in2(A[5]), .in3(A[6]), .in4(A[7]), .in5(A[8]), .in6(A[9]), .in7(A[10]),
    .in8(A[11]), .in9(A[12]), .in10(A[13]), .in11(A[14]), .in12(1'b0), .in13(1'b0), .in14(1'b0), .in15(1'b0),
    .out(Logical_Shift_Right[3]), .sel(B[3:0]));
  Multiplexer #(.select(4)) multiplexer_32 (
    .in0(A[2]), .in1(A[3]), .in2(A[4]), .in3(A[5]), .in4(A[6]), .in5(A[7]), .in6(A[8]), .in7(A[9]),
    .in8(A[10]), .in9(A[11]), .in10(A[12]), .in11(A[13]), .in12(A[14]), .in13(1'b0), .in14(1'b0),
    .in15(1'b0), .out(Logical_Shift_Right[2]), .sel(B[3:0]));
  Multiplexer #(.select(4)) multiplexer_33 (
    .in0(A[1]), .in1(A[2]), .in2(A[3]), .in3(A[4]), .in4(A[5]), .in5(A[6]), .in6(A[7]), .in7(A[8]),
    .in8(A[9]), .in9(A[10]), .in10(A[11]), .in11(A[12]), .in12(A[13]), .in13(A[14]), .in14(1'b0),
    .in15(1'b0), .out(Logical_Shift_Right[1]), .sel(B[3:0]));
  Multiplexer #(.select(4)) multiplexer_34 (
    .in0(A[0]), .in1(A[1]), .in2(A[2]), .in3(A[3]), .in4(A[4]), .in5(A[5]), .in6(A[6]), .in7(A[7]),
    .in8(A[8]), .in9(A[9]), .in10(A[10]), .in11(A[11]), .in12(A[12]), .in13(A[13]), .in14(A[14]),
    .in15(1'b0), .out(Logical_Shift_Right[0]), .sel(B[3:0]));
  Multiplexer #(.select(4)) multiplexer_35 (
    .in1(A[14]), .in2(A[13]), .in3(A[12]), .in4(A[11]), .in5(A[10]), .in6(A[9]), .in7(A[8]), .in8(A[7]),
    .in9(A[6]), .in10(A[5]), .in11(A[4]), .in12(A[3]), .in13(A[2]), .in14(A[1]), .in15(A[0]), .out(COUT_SRL),
    .sel(B[3:0]));  // open: in0
  Multiplexer #(.select(4)) multiplexer_36 (
    .in0(A[14]), .in1(A[14]), .in2(A[14]), .in3(A[14]), .in4(A[14]), .in5(A[14]), .in6(A[14]), .in7(A[14]),
    .in8(A[14]), .in9(A[14]), .in10(A[14]), .in11(A[14]), .in12(A[14]), .in13(A[14]), .in14(A[14]),
    .in15(A[14]), .out(Arithmetic_Shift_Right[14]), .sel(B[3:0]));
  Multiplexer #(.select(4)) multiplexer_37 (
    .in0(A[13]), .in1(A[14]), .in2(A[14]), .in3(A[14]), .in4(A[14]), .in5(A[14]), .in6(A[14]), .in7(A[14]),
    .in8(A[14]), .in9(A[14]), .in10(A[14]), .in11(A[14]), .in12(A[14]), .in13(A[14]), .in14(A[14]),
    .in15(A[14]), .out(Arithmetic_Shift_Right[13]), .sel(B[3:0]));
  Multiplexer #(.select(4)) multiplexer_38 (
    .in0(A[12]), .in1(A[13]), .in2(A[14]), .in3(A[14]), .in4(A[14]), .in5(A[14]), .in6(A[14]), .in7(A[14]),
    .in8(A[14]), .in9(A[14]), .in10(A[14]), .in11(A[14]), .in12(A[14]), .in13(A[14]), .in14(A[14]),
    .in15(A[14]), .out(Arithmetic_Shift_Right[12]), .sel(B[3:0]));
  Multiplexer #(.select(4)) multiplexer_39 (
    .in0(A[11]), .in1(A[12]), .in2(A[13]), .in3(A[14]), .in4(A[14]), .in5(A[14]), .in6(A[14]), .in7(A[14]),
    .in8(A[14]), .in9(A[14]), .in10(A[14]), .in11(A[14]), .in12(A[14]), .in13(A[14]), .in14(A[14]),
    .in15(A[14]), .out(Arithmetic_Shift_Right[11]), .sel(B[3:0]));
  Multiplexer #(.select(4)) multiplexer_40 (
    .in0(A[10]), .in1(A[11]), .in2(A[12]), .in3(A[13]), .in4(A[14]), .in5(A[14]), .in6(A[14]), .in7(A[14]),
    .in8(A[14]), .in9(A[14]), .in10(A[14]), .in11(A[14]), .in12(A[14]), .in13(A[14]), .in14(A[14]),
    .in15(A[14]), .out(Arithmetic_Shift_Right[10]), .sel(B[3:0]));
  Multiplexer #(.select(4)) multiplexer_41 (
    .in0(A[9]), .in1(A[10]), .in2(A[11]), .in3(A[12]), .in4(A[13]), .in5(A[14]), .in6(A[14]), .in7(A[14]),
    .in8(A[14]), .in9(A[14]), .in10(A[14]), .in11(A[14]), .in12(A[14]), .in13(A[14]), .in14(A[14]),
    .in15(A[14]), .out(Arithmetic_Shift_Right[9]), .sel(B[3:0]));
  Multiplexer #(.select(4)) multiplexer_42 (
    .in0(A[8]), .in1(A[9]), .in2(A[10]), .in3(A[11]), .in4(A[12]), .in5(A[13]), .in6(A[14]), .in7(A[14]),
    .in8(A[14]), .in9(A[14]), .in10(A[14]), .in11(A[14]), .in12(A[14]), .in13(A[14]), .in14(A[14]),
    .in15(A[14]), .out(Arithmetic_Shift_Right[8]), .sel(B[3:0]));
  Multiplexer #(.select(4)) multiplexer_43 (
    .in0(A[7]), .in1(A[8]), .in2(A[9]), .in3(A[10]), .in4(A[11]), .in5(A[12]), .in6(A[13]), .in7(A[14]),
    .in8(A[14]), .in9(A[14]), .in10(A[14]), .in11(A[14]), .in12(A[14]), .in13(A[14]), .in14(A[14]),
    .in15(A[14]), .out(Arithmetic_Shift_Right[7]), .sel(B[3:0]));
  Multiplexer #(.select(4)) multiplexer_44 (
    .in0(A[6]), .in1(A[7]), .in2(A[8]), .in3(A[9]), .in4(A[10]), .in5(A[11]), .in6(A[12]), .in7(A[13]),
    .in8(A[14]), .in9(A[14]), .in10(A[14]), .in11(A[14]), .in12(A[14]), .in13(A[14]), .in14(A[14]),
    .in15(A[14]), .out(Arithmetic_Shift_Right[6]), .sel(B[3:0]));
  Multiplexer #(.select(4)) multiplexer_45 (
    .in0(A[5]), .in1(A[6]), .in2(A[7]), .in3(A[8]), .in4(A[9]), .in5(A[10]), .in6(A[11]), .in7(A[12]),
    .in8(A[13]), .in9(A[14]), .in10(A[14]), .in11(A[14]), .in12(A[14]), .in13(A[14]), .in14(A[14]),
    .in15(A[14]), .out(Arithmetic_Shift_Right[5]), .sel(B[3:0]));
  Multiplexer #(.select(4)) multiplexer_46 (
    .in0(A[4]), .in1(A[5]), .in2(A[6]), .in3(A[7]), .in4(A[8]), .in5(A[9]), .in6(A[10]), .in7(A[11]),
    .in8(A[12]), .in9(A[13]), .in10(A[14]), .in11(A[14]), .in12(A[14]), .in13(A[14]), .in14(A[14]),
    .in15(A[14]), .out(Arithmetic_Shift_Right[4]), .sel(B[3:0]));
  Multiplexer #(.select(4)) multiplexer_47 (
    .in0(A[3]), .in1(A[4]), .in2(A[5]), .in3(A[6]), .in4(A[7]), .in5(A[8]), .in6(A[9]), .in7(A[10]),
    .in8(A[11]), .in9(A[12]), .in10(A[13]), .in11(A[14]), .in12(A[14]), .in13(A[14]), .in14(A[14]),
    .in15(A[14]), .out(Arithmetic_Shift_Right[3]), .sel(B[3:0]));
  Multiplexer #(.select(4)) multiplexer_48 (
    .in0(A[2]), .in1(A[3]), .in2(A[4]), .in3(A[5]), .in4(A[6]), .in5(A[7]), .in6(A[8]), .in7(A[9]),
    .in8(A[10]), .in9(A[11]), .in10(A[12]), .in11(A[13]), .in12(A[14]), .in13(A[14]), .in14(A[14]),
    .in15(A[14]), .out(Arithmetic_Shift_Right[2]), .sel(B[3:0]));
  Multiplexer #(.select(4)) multiplexer_49 (
    .in0(A[1]), .in1(A[2]), .in2(A[3]), .in3(A[4]), .in4(A[5]), .in5(A[6]), .in6(A[7]), .in7(A[8]),
    .in8(A[9]), .in9(A[10]), .in10(A[11]), .in11(A[12]), .in12(A[13]), .in13(A[14]), .in14(A[14]),
    .in15(A[14]), .out(Arithmetic_Shift_Right[1]), .sel(B[3:0]));
  Multiplexer #(.select(4)) multiplexer_50 (
    .in0(A[0]), .in1(A[1]), .in2(A[2]), .in3(A[3]), .in4(A[4]), .in5(A[5]), .in6(A[6]), .in7(A[7]),
    .in8(A[8]), .in9(A[9]), .in10(A[10]), .in11(A[11]), .in12(A[12]), .in13(A[13]), .in14(A[14]),
    .in15(A[14]), .out(Arithmetic_Shift_Right[0]), .sel(B[3:0]));

  assign R[14] = N;

  // Other names for the same wires on the sheet: SRA0 = Arithmetic_Shift_Right[0]; SRA1 = Arithmetic_Shift_Right[1];
  //   SRA2 = Arithmetic_Shift_Right[2]; SRA3 = Arithmetic_Shift_Right[3]; SRA4 = Arithmetic_Shift_Right[4];
  //   SRA5 = Arithmetic_Shift_Right[5]; SRA6 = Arithmetic_Shift_Right[6]; SRA7 = Arithmetic_Shift_Right[7];
  //   SRA8 = Arithmetic_Shift_Right[8]; SRA9 = Arithmetic_Shift_Right[9]; SRA10 = Arithmetic_Shift_Right[10];
  //   SRA11 = Arithmetic_Shift_Right[11]; SRA12 = Arithmetic_Shift_Right[12]; SRA13 = Arithmetic_Shift_Right[13];
  //   SRA14 = Arithmetic_Shift_Right[14]; SHFTAMT[3:0] = B[3:0]; SLL0 = Logical_Shift_Left[0];
  //   SLL1 = Logical_Shift_Left[1]; SLL2 = Logical_Shift_Left[2]; SLL3 = Logical_Shift_Left[3];
  //   SLL4 = Logical_Shift_Left[4]; SLL5 = Logical_Shift_Left[5]; SLL6 = Logical_Shift_Left[6];
  //   SLL7 = Logical_Shift_Left[7]; SLL8 = Logical_Shift_Left[8]; SLL9 = Logical_Shift_Left[9];
  //   SLL10 = Logical_Shift_Left[10]; SLL11 = Logical_Shift_Left[11]; SLL12 = Logical_Shift_Left[12];
  //   SLL13 = Logical_Shift_Left[13]; SLL14 = Logical_Shift_Left[14]; SRL0 = Logical_Shift_Right[0];
  //   SRL1 = Logical_Shift_Right[1]; SRL2 = Logical_Shift_Right[2]; SRL3 = Logical_Shift_Right[3];
  //   SRL4 = Logical_Shift_Right[4]; SRL5 = Logical_Shift_Right[5]; SRL6 = Logical_Shift_Right[6];
  //   SRL7 = Logical_Shift_Right[7]; SRL8 = Logical_Shift_Right[8]; SRL9 = Logical_Shift_Right[9];
  //   SRL10 = Logical_Shift_Right[10]; SRL11 = Logical_Shift_Right[11]; SRL12 = Logical_Shift_Right[12];
  //   SRL13 = Logical_Shift_Right[13]; SRL14 = Logical_Shift_Right[14]; R14 = N

  // Notes on the sheet:
  //   Logical Left Shifter
  //   O FLAG 
  //   C FLAG 
  //   Z FLAG 
  //   Logical Right Shifter
  //   N FLAG 
  //   Arithmetic Right Shifter
endmodule

module FLAGS8 (
  input  IRQ,
  input  [7:0] NF,
  input  [7:0] WM,
  input  CLK,
  output [7:0] F
);

  wire [7:0] SETFLAG;

  and and_1 (SETFLAG[7], WM[7], NF[7]);
  and and_2 (SETFLAG[6], WM[6], NF[6]);
  and and_3 (SETFLAG[5], WM[5], NF[5]);
  and and_4 (SETFLAG[4], WM[4], NF[4]);
  and and_5 (SETFLAG[3], WM[3], NF[3]);
  and and_6 (SETFLAG[2], WM[2], NF[2]);
  and and_7 (SETFLAG[1], WM[1], NF[1]);
  Register register_1 (.D(SETFLAG), .Q(F), .clk(CLK));  // open: en, clr
  and and_8 (SETFLAG[0], WM[0], NF[0]);
endmodule

module IMM15 (
  input  [14:0] INST,
  output [14:0] SEXT
);

  wire and_2_out, and_4_out, and_9_out, and_10_out, and_11_out, and_12_out, and_13_out, E0, E1, E2,
       IMM3_0_E2_E1_E0, IMM3_2_0_E1_E0, IMM3_2_0_E2, IMM6_0_E1, IMM6_0_E2_E0, IMM9_0_E0, IMM9_0_E2_E1,
       IMM10_4_E1_E0, IMM10_4_E2, nor_1_out, nor_2_out, nor_3_out, nor_4_out, nor_5_out, nor_6_out,
       nor_7_out, nor_8_out, nor_9_out, nor_10_out, not_1_out, not_2_out, not_3_out, not_4_out, not_5_out,
       not_6_out, not_7_out, not_8_out, not_9_out, not_10_out, not_11_out, not_12_out, not_13_out,
       not_14_out, not_15_out, not_16_out, not_17_out, not_18_out, not_19_out, not_20_out, not_21_out,
       not_22_out, not_23_out, or_1_out, or_2_out, or_3_out, or_4_out, SELECT_E0, SELECT_E1, SELECT_E2;

  Multiplexer #(.select(3), .width(15)) multiplexer_1 (
    .in0({{12{INST[14]}}, INST[13:11]}), .in1({{6{INST[14]}}, INST[13:5]}),
    .in2({{9{INST[14]}}, INST[13:8]}), .in3({{12{INST[14]}}, INST[7:5]}),
    .in4({{5{INST[14]}}, INST[13:8], 4'b0000}), .out(SEXT), .sel({SELECT_E2, SELECT_E1, SELECT_E0}));  // open: in5, in6, in7
  not not_1 (not_1_out, INST[3]);
  not not_2 (not_2_out, INST[4]);
  not not_3 (not_3_out, INST[3]);
  not not_4 (not_4_out, INST[1]);
  not not_5 (not_5_out, INST[0]);
  not not_6 (not_6_out, INST[4]);
  not not_7 (not_7_out, INST[3]);
  not not_8 (not_8_out, INST[1]);
  not not_9 (not_9_out, INST[2]);
  or or_1 (or_1_out, INST[4], not_1_out);
  or or_2 (or_2_out, INST[3], not_6_out);
  and and_1 (IMM9_0_E2_E1, or_2_out, INST[1]);
  and and_2 (and_2_out, INST[4], not_7_out);
  and and_3 (IMM9_0_E0, and_2_out, or_3_out);
  or or_3 (or_3_out, not_8_out, not_9_out);
  not not_10 (not_10_out, INST[4]);
  not not_11 (not_11_out, INST[3]);
  not not_12 (not_12_out, INST[2]);
  not not_13 (not_13_out, INST[1]);
  buf and_4 (and_4_out, or_1_out);  // AND_Gate
  or or_4 (or_4_out, not_2_out, not_3_out, INST[2], not_4_out, not_5_out);
  or or_5 (IMM6_0_E2_E0, not_10_out, not_11_out, not_12_out, INST[1]);
  and and_5 (IMM6_0_E1, INST[4], INST[3], INST[2], not_13_out);
  and and_6 (IMM3_0_E2_E1_E0, and_4_out, or_4_out);
  not not_14 (not_14_out, INST[3]);
  not not_15 (not_15_out, INST[1]);
  not not_16 (not_16_out, INST[0]);
  not not_17 (not_17_out, INST[4]);
  not not_18 (not_18_out, INST[3]);
  not not_19 (not_19_out, INST[2]);
  not not_20 (not_20_out, INST[1]);
  not not_21 (not_21_out, INST[0]);
  not not_22 (not_22_out, INST[4]);
  not not_23 (not_23_out, INST[2]);
  and and_7 (IMM10_4_E2, INST[4], INST[3], INST[2], INST[1], INST[0]);
  or or_6 (IMM10_4_E1_E0, not_17_out, not_18_out, not_19_out, not_20_out, not_21_out);
  or or_7 (IMM3_2_0_E2, not_22_out, not_14_out, not_23_out, not_15_out, INST[0]);
  and and_8 (IMM3_2_0_E1_E0, INST[4], INST[3], INST[2], INST[1], not_16_out);
  or or_8 (E2, IMM3_0_E2_E1_E0, IMM9_0_E2_E1, IMM6_0_E2_E0, IMM3_2_0_E2, IMM10_4_E2);
  or or_9 (E1, IMM3_0_E2_E1_E0, IMM9_0_E2_E1, IMM6_0_E1, IMM3_2_0_E1_E0, IMM10_4_E1_E0);
  or or_10 (E0, IMM3_0_E2_E1_E0, IMM9_0_E0, IMM6_0_E2_E0, IMM3_2_0_E1_E0, IMM10_4_E1_E0);
  nor nor_1 (nor_1_out, IMM3_0_E2_E1_E0, E2);
  nor nor_2 (nor_2_out, IMM3_0_E2_E1_E0, E1);
  nor nor_3 (nor_3_out, IMM3_0_E2_E1_E0, E0);
  nor nor_4 (nor_4_out, IMM9_0_E2_E1, E2);
  nor nor_5 (nor_5_out, IMM9_0_E2_E1, E1);
  and and_9 (and_9_out, IMM9_0_E0, E0);
  or or_11 (SELECT_E2, nor_1_out, nor_4_out, nor_6_out, nor_8_out, and_13_out);
  or or_12 (SELECT_E1, nor_2_out, nor_5_out, and_10_out, and_11_out, nor_9_out);
  or or_13 (SELECT_E0, nor_3_out, and_9_out, nor_7_out, and_12_out, nor_10_out);
  nor nor_6 (nor_6_out, IMM6_0_E2_E0, E2);
  and and_10 (and_10_out, IMM6_0_E1, E1);
  nor nor_7 (nor_7_out, IMM6_0_E2_E0, E0);
  nor nor_8 (nor_8_out, IMM3_2_0_E1_E0, E2);
  and and_11 (and_11_out, IMM3_2_0_E1_E0, E1);
  and and_12 (and_12_out, IMM3_2_0_E1_E0, E0);
  and and_13 (and_13_out, IMM10_4_E2, E2);
  nor nor_9 (nor_9_out, IMM10_4_E2, E1);
  nor nor_10 (nor_10_out, IMM10_4_E1_E0, E0);

  // Other names for the same wires on the sheet: B13 = INST[13]; IMM3_0[14:0] = {{12{INST[14]}}, INST[13:11]};
  //   IMM6_0[14:0] = {{9{INST[14]}}, INST[13:8]}; IMM9_0[14:0] = {{6{INST[14]}}, INST[13:5]};
  //   IMM10_4[14:4] = {{5{INST[14]}}, INST[13:8]}; B5 = INST[5]; IMM3_2_0[14:0] = {{12{INST[14]}}, INST[7:5]};
  //   B6 = INST[6]; B7 = INST[7]; B14 = INST[14]; B9 = INST[9]; B10 = INST[10]; B11 = INST[11]; B12 = INST[12];
  //   B8 = INST[8]; B0 = INST[0]; B1 = INST[1]; B2 = INST[2]; B3 = INST[3]; B4 = INST[4]

  // Notes on the sheet:
  //   IMM3:0 Sign Extend
  //   IMM3:0 Encoding (000)
  //   IMM9:0 Encoding (001)
  //   IMM6:0 Encoding (010)
  //   Encoded OPCODES
  //   IMM3:2:0 Encoding (011)
  //   IMM10:4 Encoding (100)
  //   Encoding for mux
endmodule

module DECODE15 (
  input  [4:0] OPCODE,
  output SWI,
  output STORE,
  output LOAD,
  output [1:0] ASEL,
  output [1:0] BSEL,
  output [2:0] ALUOP,
  output [2:0] REGDATASRC,
  output REGW,
  output [1:0] FLAGSRC,
  output [7:0] FLAGWM,
  output SRPW,
  output SRFW
);

  wire and_2_out, and_3_out, and_4_out, and_5_out, and_6_out, and_7_out, and_11_out, and_12_out, and_14_out,
       and_15_out, and_16_out, and_17_out, and_18_out, and_19_out, and_20_out, and_22_out, and_23_out,
       and_24_out, and_25_out, and_26_out, and_27_out, and_28_out, and_29_out, not_1_out, not_2_out,
       not_3_out, not_4_out, not_5_out, not_6_out, not_7_out, not_8_out, not_9_out, not_10_out, not_11_out,
       not_12_out, not_13_out, not_14_out, not_15_out, not_16_out, not_17_out, not_18_out, not_19_out,
       not_20_out, not_21_out, not_22_out, not_23_out, not_24_out, not_25_out, not_26_out, not_27_out,
       not_28_out, not_29_out, not_30_out, not_31_out, not_32_out, not_33_out, not_34_out, not_35_out,
       not_36_out, not_37_out, not_38_out, not_39_out, not_40_out, not_41_out, not_42_out, not_43_out,
       not_44_out, not_45_out, not_46_out, not_47_out, not_48_out, not_49_out, not_50_out, not_51_out,
       not_52_out, not_53_out, not_54_out, or_3_out, or_8_out;

  not not_1 (not_1_out, OPCODE[4]);
  not not_2 (not_2_out, OPCODE[4]);
  not not_3 (not_3_out, OPCODE[3]);
  not not_4 (not_4_out, OPCODE[4]);
  not not_5 (not_5_out, OPCODE[1]);
  not not_6 (not_6_out, OPCODE[4]);
  not not_7 (not_7_out, OPCODE[3]);
  not not_8 (not_8_out, OPCODE[4]);
  not not_9 (not_9_out, OPCODE[4]);
  and and_1 (ALUOP[2], not_1_out, OPCODE[2]);
  and and_2 (and_2_out, not_2_out, not_3_out, OPCODE[1]);
  and and_3 (and_3_out, not_4_out, OPCODE[3], OPCODE[2], not_5_out);
  not not_10 (not_10_out, OPCODE[4]);
  and and_4 (and_4_out, not_10_out, OPCODE[3], not_11_out, OPCODE[1]);
  not not_11 (not_11_out, OPCODE[2]);
  and and_5 (and_5_out, not_6_out, not_7_out, OPCODE[0]);
  and and_6 (and_6_out, not_8_out, OPCODE[2], OPCODE[0]);
  and and_7 (and_7_out, not_9_out, OPCODE[1], OPCODE[0]);
  // OR_Gate or_1 has open pins: in0=and_2_out, in1=and_3_out, in2=and_4_out, out=open
  or or_2 (ALUOP[0], and_5_out, and_6_out, and_7_out);
  not not_12 (not_12_out, OPCODE[4]);
  and and_8 (ALUOP[1], not_12_out, OPCODE[1]);
  not not_13 (not_13_out, OPCODE[4]);
  not not_14 (not_14_out, OPCODE[2]);
  not not_15 (not_15_out, OPCODE[1]);
  and and_9 (REGDATASRC[0], not_13_out, OPCODE[3], not_14_out, not_15_out, OPCODE[0]);
  not not_16 (not_16_out, OPCODE[4]);
  not not_17 (not_17_out, OPCODE[3]);
  not not_18 (not_18_out, OPCODE[2]);
  not not_19 (not_19_out, OPCODE[1]);
  not not_20 (not_20_out, OPCODE[0]);
  and and_10 (ASEL[1], OPCODE[4], or_3_out);
  or or_3 (or_3_out, not_16_out, not_17_out, not_18_out, not_19_out, not_20_out);
  not not_21 (not_21_out, OPCODE[4]);
  and and_11 (and_11_out, not_21_out, OPCODE[3], not_22_out, not_24_out, OPCODE[0]);
  not not_22 (not_22_out, OPCODE[2]);
  not not_23 (not_23_out, OPCODE[4]);
  not not_24 (not_24_out, OPCODE[1]);
  and and_12 (and_12_out, not_23_out, OPCODE[3]);
  or or_4 (BSEL[0], and_12_out, ASEL[0]);
  and and_13 (ASEL[0], OPCODE[4], OPCODE[3], OPCODE[2], OPCODE[1], OPCODE[0]);
  or or_5 (LOAD, and_11_out, and_14_out);
  and and_14 (and_14_out, OPCODE[4], OPCODE[3], OPCODE[2], OPCODE[1], OPCODE[0]);
  not not_25 (not_25_out, OPCODE[4]);
  or or_6 (REGW, not_25_out, ASEL[0]);
  not not_26 (not_26_out, OPCODE[4]);
  not not_27 (not_27_out, OPCODE[3]);
  not not_28 (not_28_out, OPCODE[2]);
  not not_29 (not_29_out, OPCODE[1]);
  not not_30 (not_30_out, OPCODE[4]);
  and and_15 (and_15_out, not_30_out, OPCODE[2], OPCODE[0]);
  not not_31 (not_31_out, OPCODE[4]);
  and and_16 (and_16_out, not_31_out, OPCODE[2], OPCODE[1]);
  not not_32 (not_32_out, OPCODE[4]);
  not not_33 (not_33_out, OPCODE[2]);
  not not_34 (not_34_out, OPCODE[1]);
  not not_35 (not_35_out, OPCODE[0]);
  and and_17 (and_17_out, not_26_out, not_27_out, not_28_out, not_29_out);
  and and_18 (and_18_out, not_32_out, OPCODE[3], not_33_out, not_34_out, not_35_out);
  not not_36 (not_36_out, OPCODE[0]);
  or or_7 (FLAGWM[2], and_17_out, and_15_out, and_16_out, and_18_out);
  not not_37 (not_37_out, OPCODE[4]);
  not not_38 (not_38_out, OPCODE[2]);
  not not_39 (not_39_out, OPCODE[1]);
  not not_40 (not_40_out, OPCODE[3]);
  and and_19 (and_19_out, OPCODE[3], not_36_out);
  and and_20 (and_20_out, not_37_out, not_38_out, not_39_out);
  or or_8 (or_8_out, not_40_out, and_19_out);
  and and_21 (FLAGWM[3], and_20_out, or_8_out);
  not not_41 (not_41_out, OPCODE[4]);
  not not_42 (not_42_out, OPCODE[1]);
  not not_43 (not_43_out, OPCODE[0]);
  not not_44 (not_44_out, OPCODE[4]);
  not not_45 (not_45_out, OPCODE[3]);
  not not_46 (not_46_out, OPCODE[4]);
  not not_47 (not_47_out, OPCODE[4]);
  and and_22 (and_22_out, not_47_out, OPCODE[1]);
  not not_48 (not_48_out, OPCODE[4]);
  not not_49 (not_49_out, OPCODE[1]);
  not not_50 (not_50_out, OPCODE[0]);
  not not_51 (not_51_out, OPCODE[4]);
  not not_52 (not_52_out, OPCODE[3]);
  not not_53 (not_53_out, OPCODE[4]);
  not not_54 (not_54_out, OPCODE[4]);
  and and_23 (and_23_out, not_54_out, OPCODE[1]);
  and and_24 (and_24_out, not_41_out, not_42_out, not_43_out);
  and and_25 (and_25_out, not_44_out, not_45_out);
  and and_26 (and_26_out, not_46_out, OPCODE[2]);
  and and_27 (and_27_out, not_48_out, not_49_out, not_50_out);
  and and_28 (and_28_out, not_51_out, not_52_out);
  and and_29 (and_29_out, not_53_out, OPCODE[2]);
  or or_9 (FLAGWM[1], and_24_out, and_25_out, and_26_out, and_22_out);
  or or_10 (FLAGWM[0], and_27_out, and_28_out, and_29_out, and_23_out);

  assign BSEL[1] = ASEL[1];
  assign FLAGSRC = {2{ASEL[1]}};
  assign FLAGWM[7:4] = {4{ASEL[1]}};
  assign REGDATASRC[2:1] = {2{ASEL[1]}};
  assign SRFW = ASEL[1];
  assign SRPW = ASEL[1];
  assign STORE = ASEL[1];
  assign SWI = ASEL[1];

  // Other names for the same wires on the sheet: AOP0 = ALUOP[0]; AOP1 = ALUOP[1]; AOP2 = ALUOP[2]; A0 = ASEL[0];
  //   ONE = ASEL[0]; B0 = BSEL[0]; FWM0 = FLAGWM[0]; FWM1 = FLAGWM[1]; FWM2 = FLAGWM[2]; FWM3 = FLAGWM[3];
  //   A1 = ASEL[1]; B1 = ASEL[1]; FSRC0 = ASEL[1]; FSRC1 = ASEL[1]; FWM4 = ASEL[1]; FWM5 = ASEL[1]; FWM6 = ASEL[1];
  //   FWM7 = ASEL[1]; R1 = ASEL[1]; R2 = ASEL[1]; ZERO = ASEL[1]; OP0 = OPCODE[0]; OP1 = OPCODE[1]; OP2 = OPCODE[2];
  //   OP3 = OPCODE[3]; OP4 = OPCODE[4]; R0 = REGDATASRC[0]

  // Notes on the sheet:
  //   Circuits for SWI STORE LOAD SRPW SRFW
  //   RegDataSRC Circuit
  //   ASEL Circuit
  //   BSEL Circuit
  //   FLAGSRC Circuit
  //   Circuit for REGW
  //   FLAGWM Circuit
endmodule
